# Fritzing sketch receptor (saved by Fritzing 0.9.3b)
breadboards: 1

parts:
  Componente1 = Arduino Nano (Rev3.0)
  Componente2 = NRF24L01+ Breakout Board

nets:
  GND: Componente1.GND, Componente2.GND
  N1: Componente1.D7, Componente2.CS
  N2: Componente1.D8, Componente2.CE
  N3: Componente1.D11/MOSI, Componente2.MOSI
  N4: Componente1.D12/MISO, Componente2.MISO
  3V3: Componente1.3V3, Componente2.VCC
  N5: Componente1.D13/SCK, Componente2.SCK

notes:
  CSN -
  7
  CE -
  8
  MISO -
  12
  MOSI -
  11
  CLOCK(SCK)
  - 13
  GND - preto
  VCC - vermelho
